# Fritzing sketch diagram (saved by Fritzing 0.9.10b)
breadboards: 1

parts:
  Part1 = Arduino Uno (Rev3)
  LED1 = RGB LED - (4 legs) [package="5 mm [THT]"]
  R1 = Resistor [tolerance=±5% power=0.25 resistance=220 package=THT]  # not connected
  R2 = Resistor [tolerance=±5% power=0.25 resistance=220 package=THT]  # not connected
  R3 = Resistor [tolerance=±5% power=0.25 resistance=220 package=THT]  # not connected

nets:
  N1: Part1.5V, LED1.common_anode

// code stored in the sketch: Untitled2.ino
int redPin = 11;
int greenPin = 10;
int bluePin = 9;
int delayTime = 1000;

//usu? komentarz dla diody ze wspóln? anod? 
#define COMMON_ANODE

void setup() 
{
pinMode(redPin, OUTPUT);
pinMode(greenPin, OUTPUT);
pinMode(bluePin, OUTPUT);
}

  void loop() 
{
    setColor(255, 0,0); //red
    delay(delayTime);
    setColor(0, 255,0); //green
    delay(delayTime); 
    setColor(0,0, 255); //blue
    delay(delayTime);
}

void setColor(int red, int green, int blue)
{
  #ifdef COMMON_ANODE
  red = 255 - red;
  green = 255 - green;
  blue = 255 - blue;
  #endif
  analogWrite(redPin, red);
  analogWrite(greenPin, green); 
  analogWrite(bluePin, blue);
}
